# Fritzing sketch Schema M-O (saved by Fritzing 0.9.3b)

parts:
  head_up/down = Basic Servo
  lighthouse = Basic Servo
  8_PCS = WS2812 RGB LED strip
  WeMos_D1_Mini1 = WeMos D1 Mini
  WeMos_D1_Mini2 = WeMos D1 Mini
  head_L/R = Basic Servo
  Motor_R/L = Basic Servo
  M1 = DC Motor
  L298N1 = L298N DC motor driver
  DC1 = DC_DC_XL4016 [chip_label=XL4016 package=board_screw]  # not connected
  J1 = XL4015 DC-DC CC CV module (blue)
  DFRobot_DFPlayer_Mini1 = DFRobot DFPlayer Mini [part_number=DFR0299]
  R1 = Rotary Potentiometer (Small) [maximum_resistance=100kΩ package=THT]
  ON/OFF = SPST Switch [package=switche-dpdt]
  Motor_ON/OFF = SPST Switch [package=switche-dpdt]
  SP1 = SPEAKER [package=pcb_mount_speaker]
  M2 = PAM8403 Stereo Amplifier [part_number=HW-104]
  SP2 = SPEAKER [package=pcb_mount_speaker]
  BATT1 = LiPoly Battery (1300mAh)
  A1 = ESP32-2432S028R
  A2 = ESP32-2432S028R

nets:
  N1: head_up/down.pulse, WeMos_D1_Mini1.D7
  GND: lighthouse.gnd, 8_PCS.GND, WeMos_D1_Mini1.G, WeMos_D1_Mini2.G, Motor_R/L.gnd, J1.pin_4, DFRobot_DFPlayer_Mini1.GND-1, DFRobot_DFPlayer_Mini1.GND-2, R1.leg2, M2.POWER-, M2.INPUTG, A1.Pin_1, A1.Pin_9, A2.Pin_1, A2.Pin_9
  VCC: lighthouse.vcc, 8_PCS.VCC, WeMos_D1_Mini1.5V, WeMos_D1_Mini2.5V, Motor_R/L.vcc, J1.pin_3, M2.POWER+, A1.Pin_12, A2.Pin_12
  N2: lighthouse.pulse, WeMos_D1_Mini1.D8
  N3: 8_PCS.DIN, WeMos_D1_Mini1.D4
  N4: WeMos_D1_Mini2.3V3, R1.leg1
  N5: WeMos_D1_Mini2.A0, R1.wiper
  N6: WeMos_D1_Mini2.D0, L298N1.IN3
  N7: WeMos_D1_Mini2.D5, L298N1.IN4
  N8: WeMos_D1_Mini2.D6, L298N1.ENB
  N9: WeMos_D1_Mini2.D7, Motor_R/L.pulse
  N10: WeMos_D1_Mini2.D8, head_L/R.pulse
  N11: WeMos_D1_Mini2.RX, DFRobot_DFPlayer_Mini1.TX
  N12: WeMos_D1_Mini2.TX, DFRobot_DFPlayer_Mini1.RX
  N13: M1.pin_1, L298N1.OUT4
  N14: M1.pin_2, L298N1.OUT3
  N15: L298N1.12V, Motor_ON/OFF.S
  N16: L298N1.GND, J1.pin_2, BATT1.negative
  N17: J1.pin_1, ON/OFF.S, Motor_ON/OFF.P
  N18: DFRobot_DFPlayer_Mini1.DAC_R, M2.INPUTR
  N19: DFRobot_DFPlayer_Mini1.DAC_L, M2.INPUTL
  N20: ON/OFF.P, BATT1.positive
  N21: SP1.+, M2.ROUT-
  N22: SP1.-, M2.ROUT+
  N23: M2.LOUT+, SP2.-
  N24: M2.LOUT-, SP2.+

custom parts:
  WS2812 RGB LED strip: WS2812 strip
  WeMos D1 Mini: The D1 mini is a mini wifi board based on ESP-8266EX.
  L298N DC motor driver: 2x DC motor driver with 78M05 positive voltage regulator (7..35 V) L298N: max 46 V, 2 A Set 5 V Enable jumper to enable 5 V regultor (needed for the L298N) and +5 V output at screw terminal or supply external +5 V at screw terminal Set ENA and/or ENB to +5 V to enable motor permanently or supply ENA and/or ENB with PWM signal IN1 and IN2 set rotation directory for motor A (OUT1/OUT2) IN2 and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
  DC_DC_XL4016: DC-DC Converter step down voltage regulator XL4016 custom sketch.
  XL4015 DC-DC CC CV module (blue): XL4015 DC-DC CC/CV module blue
  PAM8403 Stereo Amplifier: PAM8403 stereo amplifier module Descriptive words Links: PAM8403 product datasheet
  LiPoly Battery (1300mAh): Lithium Ion Polymer Battery (1300mAh)
  ESP32-2432S028R: The ESP32-2432S028R development board.
