# Fritzing sketch Schema transmitter (saved by Fritzing 0.9.3b)

parts:
  A1 = ESP32-2432S028R
  Súčiastka1 = Black Joystick KY-023
  Súčiastka2 = Black Joystick KY-023
  I_use_the_version_for_2_batteries_I_didn't_have_a_spare_wire_so_I_used_a_USB_C_cable_where_I_cut_off_the_end_and_soldered_it_to_the_UPS = 4x18650 battery shield [package=THT]
  Súčiastka3 = Adafruit ADS1115 16Bit I2C ADC [part_number="Adafruit #1085"]
  S1 = SPST Switch [package=switch-spdt-smd]

nets:
  GND: A1.Pin_5, A1.Pin_9, Súčiastka1.GND, Súčiastka2.GND, I_use_the_version_for_2_batteries_I_didn't_have_a_spare_wire_so_I_used_a_USB_C_cable_where_I_cut_off_the_end_and_soldered_it_to_the_UPS.pin_1, I_use_the_version_for_2_batteries_I_didn't_have_a_spare_wire_so_I_used_a_USB_C_cable_where_I_cut_off_the_end_and_soldered_it_to_the_UPS.pin_7, I_use_the_version_for_2_batteries_I_didn't_have_a_spare_wire_so_I_used_a_USB_C_cable_where_I_cut_off_the_end_and_soldered_it_to_the_UPS.pin_16, Súčiastka3.ADDR, Súčiastka3.GND
  N1: A1.Pin_6, Súčiastka3.SCL
  N2: A1.Pin_7, Súčiastka3.SDA
  +5V: A1.Pin_8, Súčiastka1.+5V, Súčiastka2.+5V, Súčiastka3.VDD
  N3: A1.Pin_12, S1.O
  N4: Súčiastka1.VRy, Súčiastka3.AIN1
  N5: Súčiastka1.VRx, Súčiastka3.AIN0
  N6: Súčiastka2.VRy, Súčiastka3.AIN3
  N7: Súčiastka2.VRx, Súčiastka3.AIN2
  N8: I_use_the_version_for_2_batteries_I_didn't_have_a_spare_wire_so_I_used_a_USB_C_cable_where_I_cut_off_the_end_and_soldered_it_to_the_UPS.pin_9, I_use_the_version_for_2_batteries_I_didn't_have_a_spare_wire_so_I_used_a_USB_C_cable_where_I_cut_off_the_end_and_soldered_it_to_the_UPS.pin_15, S1.P

custom parts:
  ESP32-2432S028R: The ESP32-2432S028R development board.
  Black Joystick KY-023: Description: The joystick is a combination of 2 analoog potentiometer and a digital switch. Arduino GND --> Module pin - Arduino +5V --> Module pin +5V Arduino Analoog 0 --> Module VRx Arduino Analoog 1 --> Module VRy Arduino Digital --> Module SW Dimensions: 1" x 1.25"
  4x18650 battery shield: 4x18650 Lithium Battery Shield V9 CC CV Type-C Micro USB Mobile Power Bank DIY Module 5V 3A 3V 1A for iPhone Samsung Xiaomi.
  Adafruit ADS1115 16Bit I2C ADC: For microcontrollers without an analog-to-digital converter or when you want a higher-precision ADC, the ADS1115 provides 16-bit precision at 860 samples/second over I2C. The chip can be configured as 4 single-ended input channels, or two differential channels. As a nice bonus, it even includes a programmable gain amplifier, up to x16, to help boost up smaller single/differential signals to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
